# Fritzing sketch Midterm Project (saved by Fritzing 0.9.4)
breadboards: 1

parts:
  Teensy_3_1 = Teensy 3.1
  U1 = ENCODER_RGB [package=encoder_led_2]
  WIZ820io1 = WIZ820io [part_number=WIZ820io]
  hc-sr1 = hc-sr04
  OLED_I2C1 = OLED 128x64 I2C Monochrome Display
  M1 = BMP280
  Neopixel1 = Adafruit RBG Smart Neopixel [package="DIP (Dual Inline) [THT]"]
  S1 = Pushbutton [package="[THT]"]
  S2 = Pushbutton [package="[THT]"]
  S3 = Pushbutton [package="[THT]"]
  R2 = Resistor [tolerance=±5% resistance=100 package="0805 [SMD]"]
  R3 = Resistor [tolerance=±5% resistance=100 package="0805 [SMD]"]
  R4 = Resistor [tolerance=±5% resistance=100 package="0805 [SMD]"]
  LED1 = LED - 5mm [color="Red (633nm)" package="5 mm [THT]"]
  LED2 = LED - 5mm [color="Yellow (592nm)" package="5 mm [THT]"]
  LED3 = LED - 5mm [color="Blue (470nm)" package="5 mm [THT]"]
  R5 = Resistor [tolerance=±5% resistance=100 package="0805 [SMD]"]
  R6 = Resistor [tolerance=±5% resistance=100 package="0805 [SMD]"]
  R7 = Resistor [tolerance=±5% resistance=100 package="0805 [SMD]"]

nets:
  GND: Teensy_3_1.GND, U1.C, WIZ820io1.GND, hc-sr1.GND, OLED_I2C1.GND, M1.GND, Neopixel1.G, R2.Pin_1, R3.Pin_1, R4.Pin_1, R5.Pin_1, R6.Pin_1, R7.Pin_1
  N1: Teensy_3_1.D0, hc-sr1.Trig
  N2: Teensy_3_1.D1, hc-sr1.Echo
  N3: Teensy_3_1.D2, U1.A
  N4: Teensy_3_1.D3, U1.B#2
  N5: Teensy_3_1.D6, LED3.anode
  N6: Teensy_3_1.D7, LED2.anode
  N7: Teensy_3_1.D8, LED1.anode
  N8: Teensy_3_1.D9, WIZ820io1.nRESET
  N9: Teensy_3_1.D10, WIZ820io1.nSS
  N10: Teensy_3_1.D11, WIZ820io1.MOSI
  N11: Teensy_3_1.D12, WIZ820io1.MISO
  N12: Teensy_3_1.D13, WIZ820io1.SCLK
  N13: Teensy_3_1.A4/D18, OLED_I2C1.SDA, M1.SDA
  N14: Teensy_3_1.A5/D19, OLED_I2C1.SCK
  N15: Teensy_3_1.A6/D20, Neopixel1.In
  VIN: Teensy_3_1.3V3, U1.+, WIZ820io1.VIN, OLED_I2C1.VDD, M1.VIN, Neopixel1.+, S1.Pin_3, S1.Pin_4, S2.Pin_3, S2.Pin_4, S3.Pin_3, S3.Pin_4
  VIN_2: Teensy_3_1.Vin, hc-sr1.VCC
  N16: S1.Pin_1, S1.Pin_2, R2.Pin_0
  N17: S2.Pin_1, S2.Pin_2, R3.Pin_0
  N18: S3.Pin_1, S3.Pin_2, R4.Pin_0
  N19: LED1.cathode, R5.Pin_0
  N20: LED2.cathode, R6.Pin_0
  N21: LED3.cathode, R7.Pin_0

custom parts:
  ENCODER_RGB: SparkFun RGB rotary Encoder
  BMP280: Temperature Humidity Barometric presure Sensor, I2C
  Pushbutton: A generic pushbutton.
  Pushbutton: A generic pushbutton.
  Pushbutton: A generic pushbutton.
